# Fritzing sketch exemplo1 (saved by Fritzing 0.9.2b)
breadboards: 1

parts:
  LCD1 = LCD screen
  U1 = POT [package=pot_mammoth]
  Componente1 = Arduino Uno (Rev3)
  S1 = Pushbutton [package="[THT]"]
  S2 = Pushbutton [package="[THT]"]
  S3 = Pushbutton [package="[THT]"]
  S4 = Pushbutton [package="[THT]"]
  S5 = Pushbutton [package="[THT]"]

nets:
  VSS: LCD1.VSS, LCD1.R/W, LCD1.DB0, LCD1.DB3, LCD1.LED-, U1.E, Componente1.GND, S1.Pin_3, S1.Pin_4, S2.Pin_3, S2.Pin_4, S3.Pin_3, S3.Pin_4, S4.Pin_3, S4.Pin_4, S5.Pin_3, S5.Pin_4
  VDD: LCD1.VDD, LCD1.LED+, U1.S, Componente1.5V
  N1: LCD1.V0, U1.A
  N2: LCD1.RS, Componente1.D7
  N3: LCD1.E, Componente1.D6_PWM
  N4: LCD1.DB4, Componente1.D5_PWM
  N5: LCD1.DB5, Componente1.D4
  N6: LCD1.DB6, Componente1.D3_PWM
  N7: LCD1.DB7, Componente1.D2
  N8: Componente1.D8, Componente1.D9_PWM, Componente1.D10_PWM/SS, S3.Pin_1, S3.Pin_2, S4.Pin_1, S4.Pin_2, S5.Pin_1, S5.Pin_2
  N9: Componente1.D11_PWM/MOSI, S2.Pin_1, S2.Pin_2
  N10: Componente1.D12/MISO, S1.Pin_1, S1.Pin_2

// code stored in the sketch: exemplo1.ino

